// Logisim project test.circ as structural Verilog: 1 circuit, main circuit main
module main (
  input  A,
  input  C,
  input  B,
  output out_4
);

  wire and_1_out;

  and and_1 (and_1_out, C, B);
  or or_1 (out_4, A, and_1_out);

  // Notes on the sheet:
  //   A+BC(A + C)
  //   A+BC
  //   AB'+AB+BC(A + C)
endmodule
